// Digital circuit lab2_part2.dig as structural Verilog
module lab2_part2 (
  input  in0,
  input  in1,
  input  in2,
  input  in3,
  input  signa,
  input  signb,
  input  signc,
  input  signd,
  input  signe,
  input  signf,
  input  signdp,
  input  segdp,
  output seg_a,
  output seg_f,
  output seg_b,
  output seg_g,
  output seg_e,
  output seg_c,
  output seg_d,
  output seg_dp,
  output sign_a,
  output sign_f,
  output sign_b,
  output sign_g,
  output sign_e,
  output sign_c,
  output sign_d,
  output sign_dp
);

  wire and_1_out, and_2_out, and_3_out, and_4_out, and_5_out, and_6_out, and_7_out, and_8_out, and_9_out,
       and_10_out, and_11_out, and_12_out, and_13_out, and_14_out, and_15_out, and_16_out, and_17_out,
       and_18_out, not_1_out, not_2_out, not_3_out, not_4_out;

  not not_1 (not_1_out, in3);
  not not_2 (not_2_out, in2);
  not not_3 (not_3_out, in1);
  not not_4 (not_4_out, in0);
  and and_1 (and_1_out, in3, not_2_out);
  and and_2 (and_2_out, not_1_out, in2);
  and and_3 (and_3_out, in3, in2);
  and and_4 (and_4_out, not_1_out, not_2_out);
  and and_5 (and_5_out, in3, not_4_out);
  and and_6 (and_6_out, not_1_out, in1);
  and and_7 (and_7_out, not_2_out, not_4_out);
  and and_8 (and_8_out, not_2_out, in1);
  and and_9 (and_9_out, not_2_out, not_3_out);
  and and_10 (and_10_out, in2, in1);
  and and_11 (and_11_out, in2, not_3_out);
  and and_12 (and_12_out, in1, not_4_out);
  and and_13 (and_13_out, not_3_out, not_4_out);
  and and_14 (and_14_out, and_1_out, in1);
  and and_15 (and_15_out, and_2_out, not_3_out);
  and and_16 (and_16_out, and_2_out, not_4_out);
  and and_17 (and_17_out, and_10_out, in0);
  and and_18 (and_18_out, and_11_out, in0);
  or or_1 (seg_a, and_1_out, and_6_out, and_7_out, and_18_out, and_12_out);
  or or_2 (seg_b, and_3_out, and_4_out, and_9_out, and_17_out, and_13_out);
  or or_3 (seg_c, and_2_out, and_1_out, not_3_out, in0);
  or or_4 (seg_d, and_7_out, and_8_out, and_18_out, and_12_out);
  or or_5 (seg_e, and_7_out, and_12_out);
  or or_6 (seg_f, and_15_out, and_14_out, and_16_out, and_13_out);
  or or_7 (seg_g, and_5_out, and_8_out, and_11_out, and_12_out);
  Seven_Seg seven_seg_1 (.a(signa), .b(signb), .c(signc), .d(signd), .e(signe), .f(signf), .g(in3), .dp(signdp));
  Seven_Seg seven_seg_2 (.a(seg_a), .b(seg_b), .c(seg_c), .d(seg_d), .e(seg_e), .f(seg_f), .g(seg_g), .dp(segdp));

  assign seg_dp = segdp;
  assign sign_a = signa;
  assign sign_b = signb;
  assign sign_c = signc;
  assign sign_d = signd;
  assign sign_dp = signdp;
  assign sign_e = signe;
  assign sign_f = signf;
  assign sign_g = in3;

  // Notes on the sheet:
  //   AB'
  //   A'B
  //   AB
  //   A'B'
  //   AD'
  //   A'C
  //   B'D'
  //   B'C
  //   B'C'
  //   BC
  //   BC'
  //   CD'
  //   C'D'
  //   AB'C
  //   A'BC'
  //   A'BD'
  //   BCD
  //   BC'D
  //   Interface (do not edit the content inside this box)
  //   Outputs:
  //   Inputs
  //   Sign
  //   Decimal Number
endmodule

/* Test case grading:
in3 in2 in1 in0  sign_a sign_b sign_c sign_d sign_e sign_f sign_g  seg_a seg_b seg_c seg_d seg_e seg_f seg_g
 0   0   0   0    0      0      0      0      0      0      0       1     1     1     1     1     1     0
*/
